# Fritzing sketch SmartIndustry_Sensors (saved by Fritzing 0.9.3b)
breadboards: 1

parts:
  LCD2 = LCD screen
  Part1 = Arduino Mega ADK (Rev3)
  Part2 = MQ-4
  DHT1 = DHT22 Humidity and Temperature Sensor
  PIR1 = PIR sensor
  SW-1 = Vibration sensor module
  U1 = Sharp Dust Sensor [part_number=GP2Y1010AU0F]
  F1 = Fan - Ventilador [package=THT]
  LED2 = LED - 3mm [color="Red (633nm)" package="3 mm [THT]"]
  J1 = Piezo Speaker
  U2 = POT [package=pot_mammoth]
  Part3 = Arduino Nano (Rev3.0)
  Matrix_keypad1 = KEYPAD 4x4
  SERVO1 = Tower Pro SG90 servo [part_number=101246]
  LED3 = LED - 3mm [color="Red (633nm)" package="3 mm [THT]"]
  LED4 = LED - 3mm [color="Green (570nm)" package="3 mm [THT]"]

nets:
  N1: LCD2.V0, U2.A
  N2: LCD2.RS, Part1.D6_PWM
  N3: LCD2.E, Part1.D5_PWM
  N4: LCD2.DB4, Part1.D4_PWM
  N5: LCD2.DB5, Part1.D3_PWM
  N6: LCD2.DB6, Part1.D2_PWM
  N7: LCD2.DB7, Part1.D1/TX0
  VCC: LCD2.LED-, Part1.5V, Part2.VCC, DHT1.VDD, PIR1.VDD, SW-1.vcc, U1.V-LED, U2.S
  GND: LCD2.LED+, Part1.GND, Part2.GND, DHT1.GND, PIR1.GND, SW-1.Ground, U1.LED-GND, F1.GND, LED2.cathode, J1.pin1, U2.E
  N8: Part1.A8, SW-1.Digital_output
  N9: Part1.A15, U1.Vo
  N10: Part1.A0, Part2.AO
  N11: Part1.D11_PWM, DHT1.DATA
  N12: Part1.D10_PWM, PIR1.SIG
  N13: Part1.D9_PWM, LED2.anode
  N14: Part1.D8_PWM, J1.pin2
  3V3: Part1.3V3, U1.VCC
  N15: Part1.D7_PWM, F1.5V
  N16: Part1.D52/SCK, U1.LED
  GND_2: Part3.GND, SERVO1.GND, LED3.cathode
  N17: Part3.D2, Matrix_keypad1.col4
  N18: Part3.D3, Matrix_keypad1.col3
  N19: Part3.D4, Matrix_keypad1.col2
  N20: Part3.D5, Matrix_keypad1.col1
  N21: Part3.D6, Matrix_keypad1.row4
  N22: Part3.D7, Matrix_keypad1.row3
  N23: Part3.D8, Matrix_keypad1.row2
  N24: Part3.D9, Matrix_keypad1.row1
  N25: Part3.D10, LED3.anode
  N26: Part3.D11/MOSI, LED4.cathode
  N27: Part3.D12/MISO, SERVO1.Signal
  5V: Part3.5V, SERVO1.+5V

notes:
  Gas Sensor
  Bread Borad
  Motion Sensor
  Buzzer
  Fan
  Vibration Sensor
  LCD Display
  Arduino Mega
  Dust Sensor
  Temperature Sensor
  Door Security
  4*4 Keypad
  Servo Motor
  Arduino Nano
  Potentiometer

custom parts:
  LCD screen: A standard character display, usually with 2x16 characters. Comes in many colors.
  Vibration sensor module: Single-roller type full induction trigger switch. When no vibration or tilt, the product is ON conduction state, and in the steady state, when a vibration or tilt, the switch will be rendered instantly disconnect the conductive resistance increases, generating a current pulse signal, thereby triggering circuit. The default state of the swith is close Digital output Supply voltage:3.3V-5V On-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
  Sharp Dust Sensor: Sharp GP2Y1010AU0F Dust Sensor
  Fan - Ventilador: Ventilador de 2 pines, se encuentra comunmente en computadoras de escritorio
  KEYPAD 4x4: Matrix keypad 16 buttons, 4 rows x 4 columns
  Tower Pro SG90 servo: Original file by John De Cristofaro http://www.adafruit.com/products/1449 Adafruit Feedback Servo (Small) Edited by: e-radionica.com 28/9/2015
